# Fritzing sketch sketch (saved by Fritzing 0.9.2b)
breadboards: 1

parts:
  Part1 = Arduino Mega 2560 (Rev3)
  OLED = Grove OLED 128x96
  U1 = ENCODER_2LED [package=encoder_led_2]

nets:
  N1: Part1.D21/SCL, OLED.SCL
  N2: Part1.D20/SDA, Part1.SDA, OLED.SDA
  5V: Part1.5V, OLED.VCC
  GND: Part1.GND, OLED.GND, U1.-
  N3: Part1.D2_PWM, U1.+G
  N4: Part1.D3_PWM, U1.+R
  N5: Part1.D4_PWM, U1.SW
